// Logisim project TicTacToe.circ as structural Verilog: 5 circuits, main circuit main
module main (
);

  wire button_1_out, button_2_out, button_3_out, button_4_out, button_5_out, button_6_out, button_7_out,
       button_8_out, button_9_out, button_10_out, button_11_out, button_12_out, button_13_out, button_14_out,
       button_15_out, button_16_out, button_17_out, button_18_out, playermoveaggregator_1_p1op1,
       playermoveaggregator_1_p1op2, playermoveaggregator_1_p1op3, playermoveaggregator_1_p1op4,
       playermoveaggregator_1_p1op5, playermoveaggregator_1_p1op6, playermoveaggregator_1_p1op7,
       playermoveaggregator_1_p1op8, playermoveaggregator_1_p1op9, playermoveaggregator_1_p1windetect,
       playermoveaggregator_1_p2op1, playermoveaggregator_1_p2op2, playermoveaggregator_1_p2op3,
       playermoveaggregator_1_p2op4, playermoveaggregator_1_p2op5, playermoveaggregator_1_p2op6,
       playermoveaggregator_1_p2op7, playermoveaggregator_1_p2op8, playermoveaggregator_1_p2op9,
       playermoveaggregator_1_p2windetect;

  Button button_1 (.out(button_1_out));
  Button button_2 (.out(button_2_out));
  Button button_3 (.out(button_3_out));
  Button button_4 (.out(button_4_out));
  Button button_5 (.out(button_5_out));
  Button button_6 (.out(button_6_out));
  Button button_7 (.out(button_7_out));
  Button button_8 (.out(button_8_out));
  Button button_9 (.out(button_9_out));
  Button button_10 (.out(button_10_out));
  Button button_11 (.out(button_11_out));
  Button button_12 (.out(button_12_out));
  Button button_13 (.out(button_13_out));
  Button button_14 (.out(button_14_out));
  Button button_15 (.out(button_15_out));
  Button button_16 (.out(button_16_out));
  Button button_17 (.out(button_17_out));
  Button button_18 (.out(button_18_out));
  PlayerMoveAggregator playermoveaggregator_1 (
    .p1op1(playermoveaggregator_1_p1op1), .p1op2(playermoveaggregator_1_p1op2),
    .p1op3(playermoveaggregator_1_p1op3), .P1ip1(button_1_out), .p1ip2(button_7_out), .p1ip3(button_8_out),
    .p1ip4(button_2_out), .p1ip5(button_9_out), .p1ip6(button_10_out), .p1op4(playermoveaggregator_1_p1op4),
    .p1op5(playermoveaggregator_1_p1op5), .p1op6(playermoveaggregator_1_p1op6), .p1ip7(button_3_out),
    .p1ip8(button_12_out), .p1ip9(button_11_out), .p1op7(playermoveaggregator_1_p1op7),
    .p1op8(playermoveaggregator_1_p1op8), .p1op9(playermoveaggregator_1_p1op9),
    .p2op1(playermoveaggregator_1_p2op1), .p2op2(playermoveaggregator_1_p2op2),
    .p2op3(playermoveaggregator_1_p2op3), .p2ip1(button_4_out), .p2ip2(button_13_out), .p2ip3(button_14_out),
    .p2ip4(button_5_out), .p2ip5(button_16_out), .p2ip6(button_15_out), .p2op4(playermoveaggregator_1_p2op4),
    .p2op5(playermoveaggregator_1_p2op5), .p2op6(playermoveaggregator_1_p2op6), .p2ip7(button_6_out),
    .p2ip8(button_17_out), .p2ip9(button_18_out), .p2op7(playermoveaggregator_1_p2op7),
    .p2op9(playermoveaggregator_1_p2op9), .p2op8(playermoveaggregator_1_p2op8),
    .P1WinDetect(playermoveaggregator_1_p1windetect), .P2WinDetect(playermoveaggregator_1_p2windetect));
  LED led_1 (.in(playermoveaggregator_1_p2op1));
  LED led_2 (.in(playermoveaggregator_1_p1op1));
  LED led_3 (.in(playermoveaggregator_1_p2op4));
  LED led_4 (.in(playermoveaggregator_1_p1op4));
  LED led_5 (.in(playermoveaggregator_1_p2op7));
  LED led_6 (.in(playermoveaggregator_1_p1op7));
  LED led_7 (.in(playermoveaggregator_1_p1op2));
  LED led_8 (.in(playermoveaggregator_1_p1op5));
  LED led_9 (.in(playermoveaggregator_1_p1op8));
  LED led_10 (.in(playermoveaggregator_1_p2op2));
  LED led_11 (.in(playermoveaggregator_1_p2op5));
  LED led_12 (.in(playermoveaggregator_1_p2op8));
  LED led_13 (.in(playermoveaggregator_1_p2op3));
  LED led_14 (.in(playermoveaggregator_1_p1op3));
  LED led_15 (.in(playermoveaggregator_1_p2op6));
  LED led_16 (.in(playermoveaggregator_1_p1op6));
  LED led_17 (.in(playermoveaggregator_1_p1op9));
  LED led_18 (.in(playermoveaggregator_1_p2op9));
  LED led_19 (.in(playermoveaggregator_1_p2windetect));
  LED led_20 (.in(playermoveaggregator_1_p1windetect));

  // Notes on the sheet:
  //   Player 1. Color RED
  //   Player 2. Color GREEN
  //   TIC TAC TOE GRID
  //   WINNER
endmodule

module PlayerMove (
  input  P1,
  input  P2,
  output O1,
  output O2
);

  wire and_1_out, and_2_out, not_1_out, not_2_out;

  not not_1 (not_1_out, O2);
  not not_2 (not_2_out, O1);
  and and_1 (and_1_out, P1, not_1_out);
  and and_2 (and_2_out, P2, not_2_out);
  D_Flip_Flop d_ff_1 (.clk(and_1_out), .D(and_1_out), .Q(O1));  // open: Qn, preset, en, reset
  D_Flip_Flop d_ff_2 (.clk(and_2_out), .D(and_2_out), .Q(O2));  // open: Qn, preset, en, reset
endmodule

// Player Move Controller
module PlayerMoveAggregator (
  input  P1ip1,
  input  p1ip2,
  input  p1ip3,
  input  p1ip4,
  input  p1ip5,
  input  p1ip6,
  input  p1ip7,
  input  p1ip8,
  input  p1ip9,
  input  p2ip1,
  input  p2ip2,
  input  p2ip3,
  input  p2ip4,
  input  p2ip5,
  input  p2ip6,
  input  p2ip7,
  input  p2ip8,
  input  p2ip9,
  output p1op1,
  output p1op2,
  output p1op3,
  output p1op4,
  output p1op5,
  output p1op6,
  output p1op7,
  output p1op8,
  output p1op9,
  output P1WinDetect,
  output p2op1,
  output p2op2,
  output p2op3,
  output P2WinDetect,
  output p2op4,
  output p2op5,
  output p2op6,
  output p2op7,
  output p2op9,
  output p2op8
);

  PlayerMove playermove_1 (.P1(P1ip1), .O1(p1op1), .P2(p2ip1), .O2(p2op1));
  PlayerMove playermove_2 (.P1(p1ip4), .O1(p1op4), .P2(p2ip4), .O2(p2op4));
  PlayerMove playermove_3 (.P1(p1ip7), .O1(p1op7), .P2(p2ip7), .O2(p2op7));
  PlayerMove playermove_4 (.P1(p1ip2), .O1(p1op2), .P2(p2ip2), .O2(p2op2));
  PlayerMove playermove_5 (.P1(p1ip5), .O1(p1op5), .P2(p2ip5), .O2(p2op5));
  PlayerMove playermove_6 (.P1(p1ip8), .O1(p1op8), .P2(p2ip8), .O2(p2op8));
  PlayerMove playermove_7 (.P1(p1ip3), .O1(p1op3), .P2(p2ip3), .O2(p2op3));
  PlayerMove playermove_8 (.P1(p1ip6), .O1(p1op6), .P2(p2ip6), .O2(p2op6));
  PlayerMove playermove_9 (.P1(p1ip9), .O1(p1op9), .P2(p2ip9), .O2(p2op9));
  winDetector windetector_1 (
    .i1(p1op1), .i2(p1op2), .i3(p1op3), .i4(p1op4), .i5(p1op5), .i6(p1op6), .i7(p1op7), .i8(p1op8),
    .i9(p1op9), .Op(P1WinDetect));
  winDetector windetector_2 (
    .i1(p2op1), .i2(p2op2), .i3(p2op3), .i4(p2op4), .i5(p2op5), .i6(p2op6), .i7(p2op7), .i8(p2op8),
    .i9(p2op9), .Op(P2WinDetect));
endmodule

// P1WIN
module winDetector (
  input  i1,
  input  i2,
  input  i3,
  input  i4,
  input  i5,
  input  i6,
  input  i7,
  input  i8,
  input  i9,
  output Op
);

  wire and_1_out, and_2_out, and_3_out, and_4_out, and_5_out, and_6_out, and_7_out, and_8_out;

  and and_1 (and_1_out, i1, i2, i3);
  and and_2 (and_2_out, i1, i5, i9);
  and and_3 (and_3_out, i1, i7, i4);
  and and_4 (and_4_out, i4, i5, i6);
  and and_5 (and_5_out, i2, i5, i8);
  and and_6 (and_6_out, i3, i5, i7);
  and and_7 (and_7_out, i7, i8, i9);
  and and_8 (and_8_out, i9, i3, i6);
  or or_1 (Op, and_1_out, and_2_out, and_3_out, and_4_out, and_5_out, and_6_out, and_7_out, and_8_out);
endmodule

module PlayerTurn (
  input  p1ip1,
  input  p1ip2,
  input  p1ip3,
  input  p1ip4,
  input  p1ip5,
  input  p1ip6,
  input  p1ip7,
  input  p1ip8,
  input  p1ip9,
  input  Toggle,
  input  p2ip1,
  input  p2ip2,
  input  p2ip3,
  input  p2ip4,
  input  p2ip5,
  input  p2ip6,
  input  p2ip7,
  input  p2ip8,
  input  p2ip9,
  output p1op1,
  output p1op2,
  output p1op3,
  output p1op4,
  output p1op5,
  output p1op6,
  output p1op7,
  output p1op8,
  output p1op9,
  output p2op1,
  output p2op2,
  output p2op3,
  output p2op4,
  output p2op5,
  output p2op6,
  output p2op7,
  output p2op8,
  output p2op9
);

  wire and_1_out, and_2_out, not_1_out, or_1_out, or_2_out, t_ff_1_q;

  or or_1 (or_1_out, p1ip1, p1ip2, p1ip3, p1ip4, p1ip5, p1ip6, p1ip7, p1ip8, p1ip9);
  or or_2 (or_2_out, p2ip1, p2ip2, p2ip3, p2ip4, p2ip5, p2ip6, p2ip7, p2ip8, p2ip9);
  T_Flip_Flop t_ff_1 (.clk(Toggle), .T(Toggle), .Q(t_ff_1_q));  // open: Qn, preset, reset, en
  not not_1 (not_1_out, t_ff_1_q);
  and and_1 (and_1_out, not_1_out, or_1_out);
  and and_2 (and_2_out, t_ff_1_q, or_2_out);
  and and_3 (p1op1, p1ip1, and_1_out);
  and and_4 (p1op4, p1ip4, and_1_out);
  and and_5 (p1op7, p1ip7, and_1_out);
  and and_6 (p2op1, p2ip1, and_2_out);
  and and_7 (p2op4, p2ip4, and_2_out);
  and and_8 (p2op7, p2ip7, and_2_out);
  and and_9 (p1op2, p1ip2, and_1_out);
  and and_10 (p1op5, p1ip5, and_1_out);
  and and_11 (p1op8, p1ip8, and_1_out);
  and and_12 (p2op2, p2ip2, and_2_out);
  and and_13 (p2op5, p2ip5, and_2_out);
  and and_14 (p2op8, p2ip8, and_2_out);
  and and_15 (p1op3, p1ip3, and_1_out);
  and and_16 (p1op6, p1ip6, and_1_out);
  and and_17 (p1op9, p1ip9, and_1_out);
  and and_18 (p2op3, p2ip3, and_2_out);
  and and_19 (p2op6, p2ip6, and_2_out);
  and and_20 (p2op9, p2ip9, and_2_out);
endmodule
